# Fritzing sketch Abluftsteuerung-Schaltung (saved by Fritzing 0.9.6b)

parts:
  R1 = Resistor [tolerance=±5% power=0.25 resistance=5.6k package=THT]
  R2 = Resistor [tolerance=±5% power=0.25 resistance=1.2k package=THT]
  Bauteil1 = Arduino Nano (Rev3.0)
  U1 = LM2596 step down module
  Fan = Fan - Ventilador [package=THT]
  J1 = Basic Servo
  W1209_Screw_Terminal = Camdenboss CTB0158-4 [part_number=CTB0158-4 package=THT]

nets:
  N1: R1.Pin_0, W1209_Screw_Terminal.pin1
  N2: R1.Pin_1, R2.Pin_0, Bauteil1.D2
  GND: R2.Pin_1, Bauteil1.GND, U1.IN-, U1.OUT-, Fan.GND, J1.gnd, W1209_Screw_Terminal.pin4
  N3: Bauteil1.D3, J1.pulse
  N4: Bauteil1.D4, Fan.Tacho
  N5: Bauteil1.D6, Fan.PWM
  VIN: Bauteil1.VIN, U1.OUT+, Fan.5V, J1.vcc
  N6: U1.IN+, W1209_Screw_Terminal.pin2, W1209_Screw_Terminal.pin3

custom parts:
  LM2596 step down module: LM2596 DC-DC step down power supply module 3 A.
  Fan - Ventilador: Ventilador de 2 pines, se encuentra comunmente en computadoras de escritorio
